// Logisim project BCD码转换余3码的转换器.circ as structural Verilog: 1 circuit, main circuit main
module main (
  input  in_1,
  input  in_2,
  input  in_3,
  input  in_4,
  output out_5,
  output out_6,
  output out_7,
  output out_8
);

  wire and_1_out, and_2_out, and_3_out, and_4_out, not_2_out, not_3_out, or_1_out;

  or or_1 (or_1_out, in_3, in_4);
  not not_1 (out_8, in_4);
  not not_2 (not_2_out, in_2);
  not not_3 (not_3_out, or_1_out);
  and and_1 (and_1_out, in_3, in_4);
  and and_2 (and_2_out, in_2, or_1_out);
  and and_3 (and_3_out, not_2_out, or_1_out);
  and and_4 (and_4_out, in_2, not_3_out);
  or or_2 (out_5, in_1, and_2_out);
  or or_3 (out_6, and_3_out, and_4_out);
  or or_4 (out_7, not_3_out, and_1_out);
endmodule
