// Logisim project homework1.circ as structural Verilog: 1 circuit, main circuit main
module main (
);

  wire _1_2_out, _1_3_out, _1_4_out, _1_out, _2_2_out, _2_3_out, _2_4_out, _2_out, _3_2_out, _3_3_out,
       _3_4_out, _3_out, _4_2_out, _4_3_out, _4_out, _5_2_out, _5_out, _6_out, buffer_1_out;

  LED led_1 (.in(_1_out));
  or _1 (_1_out, _1_2_out, _2_2_out, _3_2_out, _4_2_out, _5_out);
  or _2 (_2_out, _2_2_out, _3_2_out, _4_2_out, _5_out);
  LED led_2 (.in(_2_out));
  or _3 (_3_out, _3_2_out, _4_2_out, _5_out);
  LED led_3 (.in(_3_out));
  LED led_4 (.in(_4_out));
  or _4 (_4_out, _4_2_out, _5_out);
  LED led_5 (.in(buffer_1_out));
  buf buffer_1 (buffer_1_out, _5_out);
  Button _1_2 (.out(_1_2_out));
  Button _2_2 (.out(_2_2_out));
  Button _3_2 (.out(_3_2_out));
  Button _4_2 (.out(_4_2_out));
  Button _5 (.out(_5_out));
  LED led_6 (.in(_1_3_out));
  or _1_3 (_1_3_out, _4_2_out, _5_out);
  LED led_7 (.in(_2_3_out));
  or _2_3 (_2_3_out, _3_2_out, _2_2_out);
  LED led_8 (.in(_3_3_out));
  or _3_3 (_3_3_out, _5_out, _3_2_out, _1_2_out);
  or _1_4 (_1_4_out, _1_2_out, _2_2_out, _3_2_out, _4_2_out);
  or _2_4 (_2_4_out, _2_2_out, _3_2_out, _5_out);
  or _3_4 (_3_4_out, _4_2_out, _5_out);
  or _4_3 (_4_3_out, _2_2_out, _3_2_out, _4_2_out, _5_out);
  or _5_2 (_5_2_out, _2_2_out, _3_2_out, _5_out);
  or _6 (_6_out, _1_2_out, _3_2_out, _4_2_out, _5_out);
  _7_Segment_Display u_7_segment_display_1 (
    .g(_4_3_out), .f(_3_4_out), .a(_2_4_out), .b(_1_4_out), .e(_2_2_out), .d(_5_2_out), .c(_6_out));  // open: dp
endmodule
