// Logisim project 全加器.circ as structural Verilog: 4 circuits, main circuit main
module main (
  input  in_1,
  input  in_2,
  input  in_3,
  input  in_4,
  input  in_5,
  input  in_6,
  input  in_7,
  input  in_8,
  input  in_9,
  output out_10,
  output out_11,
  output out_12,
  output out_13,
  output out_14,
  output out_15
);

  wire \全加器_2_out_4 , \全加器_3_out_4 , \全加器_4_out_4 ;

  xor xor_1 (out_11, out_10, \全加器_2_out_4 );
  \全加器  \u_全加器_1  (.out_4(out_10), .in_3(\全加器_2_out_4 ), .in_1(in_1), .in_2(in_2), .out_5(out_12));
  \全加器  \u_全加器_2  (.out_4(\全加器_2_out_4 ), .in_3(\全加器_3_out_4 ), .in_1(in_3), .in_2(in_4), .out_5(out_13));
  \全加器  \u_全加器_3  (.out_4(\全加器_3_out_4 ), .in_3(\全加器_4_out_4 ), .in_1(in_5), .in_2(in_6), .out_5(out_14));
  \全加器  \u_全加器_4  (.out_4(\全加器_4_out_4 ), .in_3(in_9), .in_1(in_7), .in_2(in_8), .out_5(out_15));
endmodule

module \半加器  (
  input  in_1,
  input  in_2,
  output out_3,
  output out_4
);

  and and_1 (out_3, in_1, in_2);
  xor xor_1 (out_4, in_1, in_2);
endmodule

module \全加器  (
  input  in_1,
  input  in_2,
  input  in_3,
  output out_4,
  output out_5
);

  wire \半加器_1_out_3 , \半加器_1_out_4 , \半加器_2_out_3 ;

  or or_1 (out_4, \半加器_1_out_3 , \半加器_2_out_3 );
  \半加器  \u_半加器_1  (.out_3(\半加器_1_out_3 ), .in_1(in_1), .in_2(in_2), .out_4(\半加器_1_out_4 ));
  \半加器  \u_半加器_2  (.out_3(\半加器_2_out_3 ), .in_1(\半加器_1_out_4 ), .in_2(in_3), .out_4(out_5));
endmodule

module \加法器_减法器  (
  input  in_1,
  input  in_2,
  input  in_3,
  input  in_4,
  input  in_5,
  input  in_6,
  input  in_7,
  input  in_8,
  input  in_9,
  output out_10,
  output out_11,
  output out_12,
  output out_13,
  output out_14,
  output out_15
);

  wire xor_2_out, xor_3_out, xor_4_out, xor_5_out, \全加器_2_out_4 , \全加器_3_out_4 , \全加器_4_out_4 ;

  xor xor_1 (out_11, out_10, \全加器_2_out_4 );
  xor xor_2 (xor_2_out, in_9, in_2);
  \全加器  \u_全加器_1  (.out_4(out_10), .in_3(\全加器_2_out_4 ), .in_1(in_1), .in_2(xor_2_out), .out_5(out_12));
  xor xor_3 (xor_3_out, in_9, in_4);
  \全加器  \u_全加器_2  (.out_4(\全加器_2_out_4 ), .in_3(\全加器_3_out_4 ), .in_1(in_3), .in_2(xor_3_out), .out_5(out_13));
  xor xor_4 (xor_4_out, in_9, in_6);
  \全加器  \u_全加器_3  (.out_4(\全加器_3_out_4 ), .in_3(\全加器_4_out_4 ), .in_1(in_5), .in_2(xor_4_out), .out_5(out_14));
  xor xor_5 (xor_5_out, in_9, in_8);
  \全加器  \u_全加器_4  (.out_4(\全加器_4_out_4 ), .in_3(in_9), .in_1(in_7), .in_2(xor_5_out), .out_5(out_15));
endmodule
