// Logisim project 基本时序电路.circ as structural Verilog
module \SR锁存器  (
  input  in_1,
  input  in_2,
  output out_3,
  output out_4
);

  nor nor_1 (out_3, in_1, out_4);
  nor nor_2 (out_4, out_3, in_2);
endmodule

module \D锁存器  (
  input  in_1,
  input  in_2,
  output out_3,
  output out_4
);

  wire and_1_out, and_2_out, not_1_out;

  not not_1 (not_1_out, in_2);
  and and_1 (and_1_out, in_1, not_1_out);
  and and_2 (and_2_out, in_1, in_2);
  \SR锁存器  \sr锁存器_1  (.in_1(and_1_out), .in_2(and_2_out), .out_3(out_3), .out_4(out_4));
endmodule

module \D触发器  (
  input  in_1,
  input  in_2,
  output out_3,
  output out_4
);

  wire \d锁存器_1_out_3 , \d锁存器_1_out_4 , not_1_out;

  not not_1 (not_1_out, in_1);
  \D锁存器  \d锁存器_1  (.in_2(in_2), .out_3(\d锁存器_1_out_3 ), .out_4(\d锁存器_1_out_4 ), .in_1(not_1_out));
  \D锁存器  \d锁存器_2  (.in_2(\d锁存器_1_out_3 ), .out_3(out_3), .out_4(out_4), .in_1(in_1));
endmodule

module \带使能端的触发器  (
  input  in_1,
  input  in_2,
  output out_3
);

  wire clock_1_out, multiplexer_1_out;

  Multiplexer #(.disabled(0)) multiplexer_1 (.in0(out_3), .in1(in_1), .out(multiplexer_1_out), .sel(1'b1), .en(in_2));
  \D锁存器调整  \d锁存器调整_1  (.in_2(multiplexer_1_out), .out_3(out_3), .in_1(clock_1_out));
  Clock clock_1 (.out(clock_1_out));
endmodule

module \D锁存器调整  (
  input  in_1,
  input  in_2,
  output out_3
);

  wire \d锁存器_1_out_3 , \d锁存器_1_out_4 , \d锁存器_2_out_4 , not_1_out;

  not not_1 (not_1_out, in_1);
  \D锁存器  \d锁存器_1  (.in_2(in_2), .out_3(\d锁存器_1_out_3 ), .out_4(\d锁存器_1_out_4 ), .in_1(not_1_out));
  \D锁存器  \d锁存器_2  (.in_2(\d锁存器_1_out_3 ), .out_3(out_3), .out_4(\d锁存器_2_out_4 ), .in_1(in_1));
endmodule

module \带复位功能的触发器  (
  input  in_1,
  input  in_2,
  output out_3
);

  wire and_1_out, clock_1_out, not_1_out;

  not not_1 (not_1_out, in_2);
  and and_1 (and_1_out, in_1, not_1_out);
  \D锁存器调整  \d锁存器调整_1  (.in_2(and_1_out), .out_3(out_3), .in_1(clock_1_out));
  Clock clock_1 (.out(clock_1_out));
endmodule
