// Logisim project 多路选择器.circ as structural Verilog: 4 circuits, main circuit main
module main (
  input  x1,
  input  x2,
  input  s,
  input  x1_2,
  input  s_2,
  input  x2_2
);

  wire and_1_out, and_2_out, multiplexer_1_out, not_1_out, or_1_out;

  not not_1 (not_1_out, s_2);
  LED led_1 (.in(multiplexer_1_out));
  Multiplexer #(.disabled(0), .enable("false")) multiplexer_1 (.in0(x1), .in1(x2), .out(multiplexer_1_out), .sel(s));
  and and_1 (and_1_out, x1_2, not_1_out);
  and and_2 (and_2_out, s_2, x2_2);
  or or_1 (or_1_out, and_1_out, and_2_out);
  LED led_2 (.in(or_1_out));

  // Notes on the sheet:
  //   f
  //   f
endmodule

module \_4_1多路选择器  (
  input  in_1,
  input  in_2,
  input  in_3,
  input  in_4,
  input  in_5,
  input  in_6,
  output out_7
);

  wire \n2_1多路选择器_1_out_4 , \n2_1多路选择器_2_out_4 ;

  \_2_1多路选择器  \u_2_1多路选择器_1  (.in_1(in_3), .in_2(in_2), .in_3(in_4), .out_4(\n2_1多路选择器_1_out_4 ));
  \_2_1多路选择器  \u_2_1多路选择器_2  (.in_1(in_5), .in_2(in_2), .in_3(in_6), .out_4(\n2_1多路选择器_2_out_4 ));
  \_2_1多路选择器  \u_2_1多路选择器_3  (.in_1(\n2_1多路选择器_1_out_4 ), .in_2(in_1), .in_3(\n2_1多路选择器_2_out_4 ), .out_4(out_7));
endmodule

module \_2_1多路选择器  (
  input  in_1,
  input  in_2,
  input  in_3,
  output out_4
);

  wire and_1_out, and_2_out, not_1_out;

  not not_1 (not_1_out, in_2);
  and and_1 (and_1_out, in_1, not_1_out);
  and and_2 (and_2_out, in_2, in_3);
  or or_1 (out_4, and_1_out, and_2_out);
endmodule

module \_16_1多路选择器  (
  input  in_1,
  input  in_2,
  input  in_3,
  input  in_4,
  input  in_5,
  input  in_6,
  input  in_7,
  input  in_8,
  input  in_9,
  input  in_10,
  input  in_11,
  input  in_12,
  input  in_13,
  input  in_14,
  input  in_15,
  input  in_16,
  input  in_17,
  input  in_18,
  input  in_19,
  input  in_20,
  output out_21
);

  wire \n4_1多路选择器_1_out_7 , \n4_1多路选择器_2_out_7 , \n4_1多路选择器_3_out_7 , \n4_1多路选择器_4_out_7 ;

  \_4_1多路选择器  \u_4_1多路选择器_1  (
    .in_1(in_2), .in_2(in_1), .in_3(in_3), .in_4(in_4), .in_5(in_7), .in_6(in_8), .out_7(\n4_1多路选择器_1_out_7 ));
  \_4_1多路选择器  \u_4_1多路选择器_2  (
    .in_1(in_2), .in_2(in_1), .in_3(in_9), .in_4(in_10), .in_5(in_11), .in_6(in_12),
    .out_7(\n4_1多路选择器_2_out_7 ));
  \_4_1多路选择器  \u_4_1多路选择器_3  (
    .in_1(in_2), .in_2(in_1), .in_3(in_13), .in_4(in_14), .in_5(in_15), .in_6(in_16),
    .out_7(\n4_1多路选择器_3_out_7 ));
  \_4_1多路选择器  \u_4_1多路选择器_4  (
    .in_1(in_2), .in_2(in_1), .in_3(in_17), .in_4(in_18), .in_5(in_19), .in_6(in_20),
    .out_7(\n4_1多路选择器_4_out_7 ));
  \_4_1多路选择器  \u_4_1多路选择器_5  (
    .in_1(in_5), .in_2(in_6), .in_3(\n4_1多路选择器_1_out_7 ), .in_4(\n4_1多路选择器_2_out_7 ),
    .in_5(\n4_1多路选择器_3_out_7 ), .in_6(\n4_1多路选择器_4_out_7 ), .out_7(out_21));
endmodule
